# Fritzing sketch FanControlWiring (saved by Fritzing 0.9.3b)
breadboards: 1

parts:
  Q1 = NPN-Transistor [package="TO92 [THT]"]
  LED1 = LED - 5mm [color="Red (633nm)" package="5 mm [THT]"]
  R1 = Resistor [tolerance=±5% resistance=10k package="0805 [SMD]"]
  R2 = Resistor [tolerance=±5% resistance=2.2k package="0402 [SMD]"]
  R3 = Resistor [tolerance=±5% resistance=1k package="0402 [SMD]"]
  M1 = DC Motor
  R4 = Photocell (LDR) [package=THT]

nets:
  N1: Q1.E, R1.Pin_0
  N2: Q1.B, R2.Pin_1
  N3: Q1.C, R3.Pin_1
  N4: LED1.cathode, M1.pin_1, R4.pin_1
  N5: LED1.anode, R1.Pin_1, M1.pin_2
  N6: R3.Pin_0, R4.pin_0

notes:
  P0
  P1
  3V
  0V (GND)
